# Fritzing sketch fritzing (saved by Fritzing 0.9.4)
circuit board: 8.46667cm x 5.64444cm
breadboards: 1

parts:
  Part1 = Arduino Nano (Rev3.0) (ICSP)
  Part2 = adafruit [part_number="Adafruit #254"]
  VCC1 = Battery block 9V

nets:
  N1: Part1.GND, Part2.connector34, VCC1.-
  N2: Part1.D10, Part2.connector38
  N3: Part1.D11/MOSI, Part2.connector37
  N4: Part1.D12/MISO, Part2.connector36
  N5: Part1.VIN, VCC1.+
  N6: Part1.3V3, Part2.connector33
  N7: Part1.D13/SCK, Part2.connector35
